# Fritzing sketch green-thumb (saved by Fritzing 0.9.2b)
breadboards: 1

parts:
  U1 = TMP36 [package=to-92]
  LED1 = LED - 5mm [color="Red (633nm)" package="5 mm [THT]"]
  Bauteil1 = Arduino Uno (Rev3)

nets:
  N1: U1.VCC, Bauteil1.D7
  N2: U1.VOUT, Bauteil1.A0
  GND: U1.GND, Bauteil1.GND
  N3: LED1.anode, Bauteil1.D13/SCK
